# Fritzing sketch PreliminaryDesign (saved by Fritzing 0.9.3b)
breadboards: 1

parts:
  R2 = Resistor [tolerance=±5% resistance=20k package="2512 [SMD]"]
  R3 = Resistor [tolerance=±5% resistance=10k package="2512 [SMD]"]
  R4 = Resistor [tolerance=±5% resistance=10k package="2512 [SMD]"]
  R5 = Resistor [tolerance=±5% resistance=10k package="2512 [SMD]"]
  R6 = Resistor [tolerance=±5% resistance=10k package="2512 [SMD]"]
  R7 = Resistor [tolerance=±5% resistance=10k package="2512 [SMD]"]
  R8 = Resistor [tolerance=±5% resistance=10k package="2512 [SMD]"]
  R9 = Resistor [tolerance=±5% resistance=10k package="2512 [SMD]"]
  R10 = Resistor [tolerance=±5% resistance=10k package="2512 [SMD]"]
  R12 = Resistor [tolerance=±5% resistance=20k package="2512 [SMD]"]
  R13 = Resistor [tolerance=±5% resistance=20k package="2512 [SMD]"]
  R14 = Resistor [tolerance=±5% resistance=20k package="2512 [SMD]"]
  R15 = Resistor [tolerance=±5% resistance=20k package="2512 [SMD]"]
  R16 = Resistor [tolerance=±5% resistance=20k package="2512 [SMD]"]
  R17 = Resistor [tolerance=±5% resistance=20k package="2512 [SMD]"]
  R18 = Resistor [tolerance=±5% resistance=20k package="2512 [SMD]"]
  R19 = Resistor [tolerance=±5% resistance=20k package="2512 [SMD]"]
  R20 = Resistor [tolerance=±5% resistance=20k package="2512 [SMD]"]
  U1 = OP27 - Low Noise, Precision Op Amp [part_number=OP27]
  U5 = mystery part, 3 pins [chip_label="S M" part_number="Servo Motor"]
  U6 = mystery part, 3 pins [chip_label="S M" part_number="Servo Motor"]
  U7 = mystery part, 3 pins [chip_label="G S" part_number="Grey Scale"]
  U8 = mystery part, 5 pins [chip_label="L F" part_number="Line Following"]
  U9 = mystery part, 5 pins [chip_label="L F" part_number="Line Following"]
  Teensy_LC2 = Teensy LC
  SP1 = SPEAKER [package=pcb_mount_speaker]

nets:
  GND: R2.Pin_0, U1.+IN, SP1.-
  N1: R2.Pin_1, R3.Pin_0, R12.Pin_0
  N2: R3.Pin_1, R4.Pin_0, R13.Pin_0
  N3: R4.Pin_1, R5.Pin_0, R14.Pin_0
  N4: R5.Pin_1, R6.Pin_0, R15.Pin_0
  N5: R6.Pin_1, R7.Pin_0, R16.Pin_0
  N6: R7.Pin_1, R8.Pin_0, R17.Pin_0
  N7: R8.Pin_1, R9.Pin_0, R18.Pin_0
  N8: R9.Pin_1, R10.Pin_0, R19.Pin_0
  N9: R10.Pin_1, R20.Pin_0, U1.-IN
  N10: R12.Pin_1, Teensy_LC2.D2
  N11: R13.Pin_1, Teensy_LC2.A0/D14
  N12: R14.Pin_1, Teensy_LC2.D7
  N13: R15.Pin_1, Teensy_LC2.D8
  N14: R16.Pin_1, Teensy_LC2.D6
  N15: R17.Pin_1, Teensy_LC2.A6/D20
  N16: R18.Pin_1, Teensy_LC2.A7/D21
  N17: R19.Pin_1, Teensy_LC2.D5
  N18: R20.Pin_1, U1.OUT
  N19: U5.pin1, Teensy_LC2.D1
  N20: U5.pin2, U6.pin2, U7.pin3, U8.pin4, U9.pin4, Teensy_LC2.Vin
  N21: U5.pin3, U6.pin3, U7.pin2, U8.pin5, U9.pin5, Teensy_LC2.GND
  N22: U6.pin1, Teensy_LC2.D0
  N23: U7.pin1, Teensy_LC2.A1/D15
  N24: U8.pin1, Teensy_LC2.A5/D19
  N25: U8.pin2, Teensy_LC2.A8/D22
  N26: U8.pin3, Teensy_LC2.A9/D23
  N27: U9.pin1, Teensy_LC2.A2/D16
  N28: U9.pin2, Teensy_LC2.A3/D17
  N29: U9.pin3, Teensy_LC2.A4/D18

custom parts:
  Teensy LC: The Teensy is a complete USB-based microcontoller development system, in a very small footprint, capable of implementing many types of projects. All programming is done via the USB port. No special programmer is needed, only a standard micro-USB cable and a PC or Macintosh with a USB port. It has a USB keyboard/mouse/joystick emulation stack and can be programmed through Arduino IDE.
